# Fritzing sketch cooler_schematic (saved by Fritzing 0.7.10b)
breadboards: 1

parts:
  Arduino1 = Arduino
  R1 = 10k Ω Resistor [package=THT]
  M1 = DC Motor
  U1 = mystery part, 3 pins [chip_label="Hall Sensor"]

nets:
  GND: Arduino1.GND, M1.pin_2, U1.pin3
  N1: Arduino1.D2, R1.Pin_1, U1.pin1
  N2: Arduino1.+5V, R1.Pin_0
  5V: Arduino1.VIN
  12V: M1.pin_1, U1.pin2

notes:
  Pull Up resistor - 10K
