# Fritzing sketch cooler_schematic_Nokia_LCD (saved by Fritzing 0.7.10b)
breadboards: 1

parts:
  Arduino1 = Arduino
  R1 = 10k Ω Resistor [package=THT]
  M1 = DC Motor
  Hall_Sensor = Mystery Part - 2 pins [package=THT]

nets:
  GND: Arduino1.GND, M1.pin_2, Hall_Sensor.leg2
  N1: Arduino1.D2, R1.Pin_1, Hall_Sensor.leg1
  N2: Arduino1.+5V, R1.Pin_0
  5V: Arduino1.VIN
  12V: M1.pin_1

notes:
  Pull Up resistor - 10K
