# Fritzing sketch cooler_schematic_Nokia_LCD (saved by Fritzing 0.9.2b)
breadboards: 1

parts:
  Nokia_5110_LCD_Module1 = Nokia5110LCDModule
  R4 = Resistor [tolerance=±5% resistance=220 package=THT]  # not connected
  Arduino1 = Arduino Uno (Rev3)
  R5 = Resistor [tolerance=±5% resistance=10k package=THT]

nets:
  N1: Nokia_5110_LCD_Module1.Vcc, Arduino1.D12/MISO
  N2: Nokia_5110_LCD_Module1.Grnd, Arduino1.D11_PWM/MOSI
  N3: Nokia_5110_LCD_Module1.SCE, Arduino1.D10_PWM/SS
  N4: Nokia_5110_LCD_Module1.RST, Arduino1.D9_PWM
  N5: Nokia_5110_LCD_Module1.D/C, Arduino1.D8
  N6: Nokia_5110_LCD_Module1.6_DN_(MOSI), Arduino1.5V, R5.Pin_0
  N7: Nokia_5110_LCD_Module1.LED, Arduino1.GND
  N8: Arduino1.D2, R5.Pin_1

custom parts:
  : Nokia 5110 LCD with 8 pin. It's a 45mm*45mm module part. Description: The Nokia 5110 is a basic graphic LCD screen for lots of applications. It was originally intended for as a cell phone screen. This one is mounted on an easy to solder PCB. It uses the PCD8544 controller. The PCD8544 is a low power CMOS LCD controller/driver, designed to drive a graphic display of 48 rows and 84 columns. All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
